// Logisim project ULA.circ as structural Verilog: 2 circuits, main circuit main
module main (
  input  BINVERTE,
  input  [1:0] Op,
  input  B3,
  input  B2,
  input  B1,
  input  B0,
  input  A3,
  input  A2,
  input  A1,
  input  A0,
  output S0,
  output S1,
  output S2,
  output S3,
  output out_15
);

  wire alu_1_c_out, alu_2_c_out, alu_3_c_out;

  alu alu_1 (.A(A0), .B(B0), .B_INVERT(BINVERTE), .C_IN(BINVERTE), .Op(Op), .C_OUT(alu_1_c_out), .RESULTADO(S0));
  alu alu_2 (.A(A1), .B(B1), .B_INVERT(BINVERTE), .C_IN(alu_1_c_out), .Op(Op), .C_OUT(alu_2_c_out), .RESULTADO(S1));
  alu alu_3 (.A(A2), .B(B2), .B_INVERT(BINVERTE), .C_IN(alu_2_c_out), .Op(Op), .C_OUT(alu_3_c_out), .RESULTADO(S2));
  alu alu_4 (.A(A3), .B(B3), .B_INVERT(BINVERTE), .C_IN(alu_3_c_out), .Op(Op), .C_OUT(out_15), .RESULTADO(S3));

  // Notes on the sheet:
  //   ULA
  //   ULA
  //   ULA
  //   ULA
endmodule

module alu (
  input  B_INVERT,
  input  C_IN,
  input  [1:0] Op,
  input  A,
  input  B,
  output RESULTADO,
  output C_OUT
);

  wire adder_1_out, and_1_out, multiplexer_1_out, not_1_out, not_2_out, or_1_out;

  Multiplexer #(.enable("false")) multiplexer_1 (.in0(B), .in1(not_1_out), .out(multiplexer_1_out), .sel(B_INVERT));
  not not_1 (not_1_out, B);
  and and_1 (and_1_out, A, multiplexer_1_out);
  or or_1 (or_1_out, A, multiplexer_1_out);
  not not_2 (not_2_out, A);
  Adder #(.width(1)) adder_1 (.a(A), .b(multiplexer_1_out), .out(adder_1_out), .cin(C_IN), .cout(C_OUT));
  Multiplexer #(.select(2), .enable("false")) multiplexer_2 (
    .in0(and_1_out), .in1(or_1_out), .in2(not_2_out), .in3(adder_1_out), .out(RESULTADO), .sel(Op));

  // Notes on the sheet:
  //   MUX
endmodule
